# Fritzing sketch RaspiPool Extra Parts V2 (saved by Fritzing 0.9.4)

parts:
  Raspberry_Pi1 = Raspberry Pi B rev2
  RHT1 = Humidity and Temperature Sensor RHT03
  YF-S201_Flow_Meter1 = YF-S201 Water Flow Meter
  R5 = Resistor [tolerance=±5% resistance=10k package=THT]
  U1 = 4RelayModule
  pH_Circuit1 = pH Circuit
  ORP_Circuit1 = ORP Circuit
  U2 = BNC socket [package=bnc]  # not connected
  U3 = BNC socket [package=bnc]  # not connected
  FLO-30_Circuit1 = FLO-30 Circuit
  U4 = BNC socket [package=bnc]  # not connected
  U5 = RJ45 Jack [package=rj45-8]  # not connected
  Raspberry_Pi_1 = Raspberry Pi 3 [part_number=RPI-3-V1.2]  # not connected
  M1 = DC Motor  # not connected
  Part1 = MCP9808 High Accuracy I2C Temperature Sensor [part_number=1782]
  M3 = DC Motor  # not connected
  Grove1 = Grove 3 Axis Digital Accelerometer 16g  # not connected

nets:
  VCC: Raspberry_Pi1.3V3, Raspberry_Pi1.5V, Raspberry_Pi1.GPIO_2, Raspberry_Pi1.GPIO_24, RHT1.Vcc, YF-S201_Flow_Meter1.SIG, YF-S201_Flow_Meter1.VCC, R5.Pin_1, U1.VCC, Part1.VDD, Part1.SDA
  GND: Raspberry_Pi1.GPIO_3, Raspberry_Pi1.GND, Raspberry_Pi1.GPIO_10, Raspberry_Pi1.GPIO_7, RHT1.GND_2, YF-S201_Flow_Meter1.GND, U1.GND, pH_Circuit1.GND, ORP_Circuit1.GND, FLO-30_Circuit1.GND, Part1.SCL
  N1: Raspberry_Pi1.GPIO_23, RHT1.Data-signal, R5.Pin_0
  N2: Raspberry_Pi1.GPIO_14, pH_Circuit1.TX, ORP_Circuit1.TX, FLO-30_Circuit1.TX
  N3: Raspberry_Pi1.GPIO_15, pH_Circuit1.RX, ORP_Circuit1.RX, FLO-30_Circuit1.RX
  N4: Raspberry_Pi1.GPIO_17, Raspberry_Pi1.GPIO_18, U1.IN1
  N5: Raspberry_Pi1.GPIO_27, U1.IN2
  N6: Raspberry_Pi1.GPIO_22, U1.IN3
  N7: Raspberry_Pi1.GPIO_9, Raspberry_Pi1.GPIO_25, U1.IN4

notes:
  17
  27
  22
  25
  24
  23
  pH
  ORP
  RTD
  2 relay brd
  1 (W/Or) => black
  2 (Or/W) => brown
  3 (W/Gr) => red
  4 (B/W) => orange
  5 (W/B) => yellow
  6 (Gr/W) => green
  pH- Pump
  pH Pump
  Via Tentacle HAT
  Cl Pump
  Pump
  Speed2
  Light
  Ezo 12V

custom parts:
  YF-S201 Water Flow Meter: The YF-S201 Flow Meter. The input voltage is 5V to 24V (DC).
  4RelayModule: 4 relay arduino module SONGLE SRD05VDC-SL-C
  MCP9808 High Accuracy I2C Temperature Sensor: This I2C digital temperature sensor is one of the more accurate/precise we've ever seen, with a typical accuracy of ±0.25°C over the sensor's -40°C to +125°C range and precision of +0.0625°C. They work great with any microcontroller using standard i2c. There are 3 address pins so you can connect up to 8 to a single I2C bus without address collisions. Best of all, a wide voltage range makes is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
